# Fritzing sketch red_led_on_dout13 (saved by Fritzing 0.9.1b)
breadboards: 1

parts:
  LED1 = LED - 5mm [color="Red (633nm)" package="5 mm [THT]"]
  Part4 = Arduino Uno (Rev3)
  R2 = Resistor [tolerance=±5% resistance=1k package=THT]

nets:
  N1: LED1.cathode, Part4.D13/SCK
  N2: LED1.anode, R2.Pin_0
  N3: Part4.GND, R2.Pin_1
