# Fritzing sketch three_buttons_three_leds (saved by Fritzing 0.9.1b)
breadboards: 1

parts:
  S1 = Pushbutton [package="[THT]"]
  S5 = Pushbutton [package="[THT]"]
  S6 = Pushbutton [package="[THT]"]
  R1 = Resistor [tolerance=±5% resistance=330 package=THT]
  LED1 = LED - 5mm [color="Red (633nm)" package="5 mm [THT]"]
  LED2 = LED - 5mm [color="Red (633nm)" package="5 mm [THT]"]
  LED3 = LED - 5mm [color="Red (633nm)" package="5 mm [THT]"]
  R2 = Resistor [tolerance=±5% resistance=330 package=THT]
  R3 = Resistor [tolerance=±5% resistance=330 package=THT]
  Arduino1 = Arduino Uno (Rev3)

nets:
  N1: S1.Pin_1, S1.Pin_2
  N2: S1.Pin_3, S1.Pin_4, S5.Pin_3, S5.Pin_4, S6.Pin_3, S6.Pin_4, LED1.cathode, LED2.cathode, LED3.cathode, Arduino1.GND
  N3: S5.Pin_1, S5.Pin_2
  N4: S6.Pin_1, S6.Pin_2
  N5: R1.Pin_0, LED1.anode
  N6: R1.Pin_1, Arduino1.D6_PWM
  N7: LED2.anode, R2.Pin_0
  N8: LED3.anode, R3.Pin_0
  N9: R2.Pin_1, Arduino1.D5_PWM
  N10: R3.Pin_1, Arduino1.D3_PWM

notes:
  BOM:
  - Arduino UNO
  - Button (x 3)
  - Resistor 330 ohm (x 3)
  - Red LED (x 3)
  - Mini Breadboard
