# Fritzing sketch actuonix_feedback (saved by Fritzing 0.9.9b)
breadboards: 2
perfboards: 2

parts:
  J1 = Camdenboss CTB0158-5 [part_number=CTB0158-5 package=THT]  # not connected
  J2 = Camdenboss CTB0158-5 [part_number=CTB0158-5 package=THT]  # not connected
  J3 = female pin header, 12 pins [form="♀ (female)"]  # not connected
  J4 = female pin header, 15 pins [form="♀ (female)"]  # not connected
  J6 = screw terminal, 4 pins  # not connected
  J7 = screw terminal, 4 pins  # not connected
  CONN1 = USB connector [package=THT]
  J8 = Dagu DGServo 9g header (male) [package=THT]  # not connected
  J9 = Dagu DGServo 9g header (male) [package=THT]
  U1 = POT [package=3362u]  # not connected
  U2 = POT [package=3362u]  # not connected
  U3 = POT [package=3362u]  # not connected
  U4 = POT [package=3362u]  # not connected
  J10 = female pin header, 5 pins [form="♀ (female)"]
  CONN2 = USB connector [package=THT]
  Grove1 = Grove OLED 128x96  # not connected
  BAT1 = Battery Holders [package=lipo-1100mAh]
  J11 = Screw terminal - 2 pins [package=THT]
  M1 = Stepper Motor - Bipolar  # not connected
  BAT2 = Battery Holders [package=battery-aa]
  BAT3 = Battery Holders [package=battery-aa]
  BAT4 = Battery Holders [package=battery-aa]
  BAT5 = Battery Holders [package=battery-aa]
  BAT6 = Battery Holders [package=battery-aa]
  BAT7 = Battery Holders [package=battery-aa]
  BAT8 = Battery Holders [package=battery-aa]
  BAT9 = Battery Holders [package=battery-aa]
  JP3 = Header 5x2 [package=2x5-ra]
  U6 = POT [package=3362u]  # not connected
  Adafruit_HUZZAH_ESP8266_Breakout1 = Adafruit HUZZAH ESP8266 Breakout [part_number=2471]  # not connected

nets:
  N1: CONN1.GND, CONN1.chassis5, CONN1.chassis6
  N2: J9.Vcc, BAT9.+
  N3: J10.pin1, JP3.1, JP3.2
  N4: J10.pin4, JP3.7, JP3.8
  N5: CONN2.GND, CONN2.chassis5, CONN2.chassis6
  N6: BAT1.+, J11.pin2
  N7: BAT2.-, BAT3.+
  N8: BAT2.+, JP3.5, JP3.6
  N9: BAT3.-, BAT4.+
  N10: BAT4.-, BAT5.+
  N11: BAT5.-, BAT6.+
  N12: BAT6.-, BAT7.+
  N13: BAT7.-, BAT8.+
  N14: BAT8.-, BAT9.-
  N15: JP3.3, JP3.4
  N16: JP3.9, JP3.10
