# Fritzing sketch one_button_three_leds (saved by Fritzing 0.9.1b)
circuit board: 8.46667cm x 5.64444cm
breadboards: 1

parts:
  LED1 = LED - 5mm [color="Green (565nm)" package="5 mm [THT]"]
  Arduino1 = Arduino Uno (Rev3)
  R1 = Resistor [tolerance=±5% resistance=820 package=THT]
  S1 = Pushbutton [package="[THT]"]
  R4 = Resistor [tolerance=±5% resistance=820k package=THT]
  LED3 = LED - 5mm [color="Red (635nm)" package="5 mm [THT]"]
  LED2 = LED - 5mm [color="Yellow (585nm)" package="5 mm [THT]"]
  R2 = Resistor [tolerance=±5% resistance=820 package=THT]
  R3 = Resistor [tolerance=±5% resistance=820 package=THT]

nets:
  N1: LED1.cathode, R1.Pin_1
  N2: LED1.anode, Arduino1.D11_PWM/MOSI
  N3: Arduino1.D9_PWM, LED3.anode
  N4: Arduino1.D10_PWM/SS, LED2.anode
  GND: Arduino1.GND, R1.Pin_0, R4.Pin_0, R2.Pin_0, R3.Pin_0
  N5: Arduino1.D7, S1.Pin_1, S1.Pin_2, R4.Pin_1
  N6: Arduino1.5V, S1.Pin_3, S1.Pin_4
  N7: LED3.cathode, R3.Pin_1
  N8: LED2.cathode, R2.Pin_1
