# Fritzing sketch sparkcore_led_temperature (saved by Fritzing 0.9.1b)
circuit board: 8.46667cm x 5.64444cm
breadboards: 1

parts:
  LED1 = LED - 5mm [color="Green (565nm)" package="5 mm [THT]"]
  R1 = Resistor [tolerance=±5% resistance=820 package=THT]
  SC1 = Spark Core (v1.0)
  T1 = LM35 Temperature Sensor [package="TO92 [THT]"]
  C1 = Capacitor [package=cap-pth-large]

nets:
  N1: LED1.cathode, R1.Pin_1
  N2: LED1.anode, SC1.D0
  GND: R1.Pin_0, SC1.GND, T1.GND, C1.2
  N3: SC1.A0, T1.Vout, C1.1
  N4: SC1.3V3*, T1.+Vs
