# Fritzing sketch three_buttons_three_leds (saved by Fritzing 0.9.1b)
circuit board: 16.9333cm x 5.64444cm
breadboards: 1

parts:
  S1 = Pushbutton [package="[THT]"]
  S2 = Pushbutton [package="[THT]"]
  S3 = Pushbutton [package="[THT]"]
  R1 = Resistor [tolerance=±5% resistance=820 package=THT]
  LED1 = LED - 5mm [color="Green (560nm)" package="5 mm [THT]"]
  LED2 = LED - 5mm [color="Yellow (592nm)" package="5 mm [THT]"]
  LED3 = LED - 5mm [color="Red (633nm)" package="5 mm [THT]"]
  R2 = Resistor [tolerance=±5% resistance=820 package=THT]
  R3 = Resistor [tolerance=±5% resistance=820 package=THT]
  Arduino1 = Arduino Uno (Rev3)

nets:
  N1: S1.Pin_1, S1.Pin_2, Arduino1.D12/MISO
  N2: S1.Pin_3, S1.Pin_4, S2.Pin_3, S2.Pin_4, S3.Pin_3, S3.Pin_4, LED1.cathode, LED2.cathode, LED3.cathode, Arduino1.GND
  N3: S2.Pin_1, S2.Pin_2, Arduino1.D11_PWM/MOSI
  N4: S3.Pin_1, S3.Pin_2, Arduino1.D10_PWM/SS
  N5: R1.Pin_0, Arduino1.D6_PWM
  N6: R1.Pin_1, LED3.anode
  N7: LED1.anode, R3.Pin_1
  N8: LED2.anode, R2.Pin_1
  N9: R2.Pin_0, Arduino1.D5_PWM
  N10: R3.Pin_0, Arduino1.D3_PWM

notes:
  BOM:
  - Arduino UNO
  - Button (x 3)
  - Resistor 330 ohm (x 3)
  - LED (x 3)
  - Mini Breadboard
